// Logisim project Decoder.dbs13.hw5.circ as structural Verilog: 1 circuit, main circuit main
module main (
);

  wire or_1_out, undriven;

  or or_1 (or_1_out, undriven, undriven, undriven, undriven, undriven);

  // Notes on the sheet:
  //   a
  //   b
  //   c
  //   m0
  //   m1
  //   m2
  //   m3
  //   m4
  //   m5
  //   m6
  //   m7
  //   X
  //   X
  //   F
endmodule
