// Logisim project dbs13.ec1.circ as structural Verilog: 1 circuit, main circuit main
module main (
);

  wire and_1_out, and_2_out, not_1_out, not_2_out, or_1_out, undriven, undriven_2, undriven_3;

  not not_1 (not_1_out, undriven_2);
  not not_2 (not_2_out, undriven_3);
  and and_1 (and_1_out, undriven, not_1_out);
  and and_2 (and_2_out, undriven, not_2_out);
  or or_1 (or_1_out, and_1_out, and_2_out);

  // Notes on the sheet:
  //   A
  //   B
  //   C
  //   F
endmodule
